# Fritzing sketch MaP-Controller-v1.0.0 (saved by Fritzing 0.9.3b)
breadboards: 1

parts:
  Part3 = Genuino 101
  Part4 = MDD10A
  M1 = DC Motor
  M2 = DC Motor
  M3 = DC Motor
  M4 = DC Motor
  M6 = DC Motor
  M7 = DC Motor
  M10 = DC Motor
  M11 = DC Motor
  VCC1 = Battery block 9V
  VCC2 = Battery
  VCC3 = Battery
  M12 = DC Motor
  M13 = DC Motor
  VCC4 = Battery
  JACK1 = 2.1mm Barrel Jack with Terminal Block
  hc-sr1 = hc-sr04

nets:
  GND: Part3.GND, Part4.no_name_yet#connectorgnd-1, hc-sr1.GND
  N1: Part3.D2, hc-sr1.Echo
  N2: Part3.D3_PWM, hc-sr1.Trig
  N3: Part3.D4, Part4.no_name_yet#connectordir-1
  N4: Part3.D5_PWM, Part4.no_name_yet#connectorpwm-1
  N5: Part3.D6_PWM, Part4.no_name_yet#connectorpwm-2
  N6: Part3.D7, Part4.no_name_yet#connectordir-2
  5V: Part3.5V, hc-sr1.VCC
  N7: Part4.no_name_yet#connectorBatt-1, VCC2.+
  N8: Part4.no_name_yet#connectorBatt-2, VCC4.-
  N9: Part4.no_name_yet#connectorM1A-1, M1.pin_2, M2.pin_2, M3.pin_2, M4.pin_2, M6.pin_2
  N10: Part4.no_name_yet#connectorM1B-1, M1.pin_1, M2.pin_1, M3.pin_1, M4.pin_1, M6.pin_1
  N11: Part4.no_name_yet#connectorM2A-1, M7.pin_2, M10.pin_2, M11.pin_2, M12.pin_2, M13.pin_2
  N12: Part4.no_name_yet#connectorM2B-1, M7.pin_1, M10.pin_1, M11.pin_1, M12.pin_1, M13.pin_1
  N13: VCC1.-, JACK1.NEG
  N14: VCC1.+, JACK1.POS
  N15: VCC2.-, VCC3.+
  N16: VCC3.-, VCC4.+

notes:
  Right Motors
  Left Motors
  Motor Driver
  Motor Batteries
  Arduino Battery
  Ultrasonic Sensor
  Mini Breadboard

custom parts:
  Genuino 101: A learning and development board that delivers the performance and low-power consumption of the Intel® Curie™ Module with the simplicity of Arduino at an entry-level price. It keeps the same robust form factor and peripheral list of the UNO with the addition of onboard Bluetooth LE capabilities and a 6-axis accelerometer/gyro to help you easily expand your creativity into the connected world.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
